// Logisim project RV32_IM.circ as structural Verilog: 4 circuits, main circuit main
module main (
);

  wire W_EN;
  wire [31:0] ADDR, DATA, INST;

  Clock clock_1 (.out(W_EN));
  CPU cpu_1 (.in_1(INST), .in_2(W_EN), .out_5(W_EN), .out_3(ADDR), .out_4(DATA));
  RAM #(.addrWidth(24), .dataWidth(32), .enables("line")) ram_1 (
    .addr(ADDR[23:0]), .we(W_EN), .clk(W_EN), .din(DATA), .dout(INST));
endmodule

module CPU (
  input  [31:0] in_1,
  input  in_2,
  output [31:0] out_3,
  output [31:0] out_4,
  output out_5
);

  wire B_beq, B_blt, B_bltu, B_TYPE, comparator_1_eq, comparator_2_eq, comparator_3_eq, comparator_4_eq,
       comparator_5_eq, comparator_6_eq, comparator_7_eq, comparator_8_eq, comparator_9_eq, comparator_10_eq,
       comparator_11_eq, comparator_12_eq, comparator_13_eq, comparator_14_eq, comparator_15_eq,
       comparator_16_eq, comparator_17_eq, comparator_18_eq, comparator_19_eq, comparator_20_eq,
       comparator_21_eq, comparator_22_eq, comparator_23_eq, comparator_24_eq, comparator_25_eq,
       comparator_26_eq, comparator_27_eq, comparator_28_eq, comparator_29_eq, comparator_30_eq,
       comparator_31_eq, comparator_32_eq, comparator_41_eq, comparator_42_eq, comparator_43_eq,
       comparator_44_eq, comparator_45_eq, comparator_46_eq, comparator_47_eq, comparator_48_eq,
       comparator_49_eq, comparator_50_eq, comparator_51_eq, comparator_52_eq, comparator_53_eq,
       comparator_54_eq, comparator_55_eq, comparator_56_eq, comparator_57_eq, comparator_58_eq, I_add,
       I_and, I_jalr, I_lb, I_lh, I_lw, I_mulh, I_or, I_rem, I_sll, I_slt, I_srl, I_TYPE, I_TYPE_LOAD,
       I_TYPE_OTHER, I_xor, isEqual, or_1_out, or_2_out, or_3_out, or_4_out, or_5_out, or_6_out, or_7_out,
       or_8_out, or_9_out, R_add, R_and, R_div, R_mul, R_mulh, R_or, R_rem, R_sll, R_slt, R_srl, R_sub,
       R_TYPE, R_xor, S_sw, S_swge, S_TYPE, U_jal, U_TYPE, U_TYPE_LOAD, undriven;
  wire [1:0] ALU_X1_SEL, ALU_X2_SEL;
  wire [2:0] Imm_SEL;
  wire [3:0] ALU_OP;
  wire [31:0] ALU_OUT, ALU_X1, ALU_X2, Imm_B, Imm_I, Imm_J, Imm_S, Imm_Value, PC_1, R1_DATA, R2_DATA,
       undriven_2;

  Comparator #(.width(3)) comparator_1 (.a(in_1[14:12]), .b(3'b000), .eq(comparator_1_eq));  // open: gt, lt
  Comparator #(.width(7)) comparator_2 (.a(in_1[31:25]), .b({7{1'b0}}), .eq(comparator_2_eq));  // open: gt, lt
  Comparator #(.width(3)) comparator_3 (.a(in_1[14:12]), .b(3'b000), .eq(comparator_3_eq));  // open: gt, lt
  Comparator #(.width(7)) comparator_4 (.a(in_1[31:25]), .b(7'b0000001), .eq(comparator_4_eq));  // open: gt, lt
  Comparator #(.width(3)) comparator_5 (.a(in_1[14:12]), .b(3'b000), .eq(comparator_5_eq));  // open: gt, lt
  Comparator #(.width(7)) comparator_6 (.a(in_1[31:25]), .b(7'b0000010), .eq(comparator_6_eq));  // open: gt, lt
  Comparator #(.width(3)) comparator_7 (.a(in_1[14:12]), .b(3'b001), .eq(comparator_7_eq));  // open: gt, lt
  Comparator #(.width(7)) comparator_8 (.a(in_1[31:25]), .b({7{1'b0}}), .eq(comparator_8_eq));  // open: gt, lt
  Comparator #(.width(3)) comparator_9 (.a(in_1[14:12]), .b(3'b001), .eq(comparator_9_eq));  // open: gt, lt
  Comparator #(.width(7)) comparator_10 (.a(in_1[31:25]), .b(7'b0000001), .eq(comparator_10_eq));  // open: gt, lt
  Comparator #(.width(3)) comparator_11 (.a(in_1[14:12]), .b(3'b010), .eq(comparator_11_eq));  // open: gt, lt
  Comparator #(.width(7)) comparator_12 (.a(in_1[31:25]), .b({7{1'b0}}), .eq(comparator_12_eq));  // open: gt, lt
  REGISTERS registers_1 (
    .in_1(in_1[19:15]), .in_2(in_1[24:20]), .in_3(undriven), .in_4(in_1[11:7]), .in_5(undriven_2),
    .in_6(in_2), .out_7(R1_DATA), .out_8(R2_DATA));
  and and_1 (R_add, R_TYPE, comparator_1_eq, comparator_2_eq);
  and and_2 (R_mul, R_TYPE, comparator_3_eq, comparator_4_eq);
  and and_3 (R_sub, R_TYPE, comparator_5_eq, comparator_6_eq);
  and and_4 (R_sll, R_TYPE, comparator_7_eq, comparator_8_eq);
  and and_5 (R_mulh, R_TYPE, comparator_9_eq, comparator_10_eq);
  and and_6 (R_slt, R_TYPE, comparator_11_eq, comparator_12_eq);
  Comparator #(.width(3)) comparator_13 (.a(in_1[14:12]), .b(3'b100), .eq(comparator_13_eq));  // open: gt, lt
  Comparator #(.width(7)) comparator_14 (.a(in_1[31:25]), .b({7{1'b0}}), .eq(comparator_14_eq));  // open: gt, lt
  Comparator #(.width(3)) comparator_15 (.a(in_1[14:12]), .b(3'b100), .eq(comparator_15_eq));  // open: gt, lt
  Comparator #(.width(7)) comparator_16 (.a(in_1[31:25]), .b(7'b0000001), .eq(comparator_16_eq));  // open: gt, lt
  Comparator #(.width(3)) comparator_17 (.a(in_1[14:12]), .b(3'b101), .eq(comparator_17_eq));  // open: gt, lt
  Comparator #(.width(7)) comparator_18 (.a(in_1[31:25]), .b({7{1'b0}}), .eq(comparator_18_eq));  // open: gt, lt
  Comparator #(.width(3)) comparator_19 (.a(in_1[14:12]), .b(3'b110), .eq(comparator_19_eq));  // open: gt, lt
  Comparator #(.width(7)) comparator_20 (.a(in_1[31:25]), .b({7{1'b0}}), .eq(comparator_20_eq));  // open: gt, lt
  Comparator #(.width(3)) comparator_21 (.a(in_1[14:12]), .b(3'b110), .eq(comparator_21_eq));  // open: gt, lt
  Comparator #(.width(7)) comparator_22 (.a(in_1[31:25]), .b(7'b0000001), .eq(comparator_22_eq));  // open: gt, lt
  Comparator #(.width(3)) comparator_23 (.a(in_1[14:12]), .b(3'b111), .eq(comparator_23_eq));  // open: gt, lt
  Comparator #(.width(7)) comparator_24 (.a(in_1[31:25]), .b({7{1'b0}}), .eq(comparator_24_eq));  // open: gt, lt
  and and_7 (R_xor, R_TYPE, comparator_13_eq, comparator_14_eq);
  and and_8 (R_div, R_TYPE, comparator_15_eq, comparator_16_eq);
  and and_9 (R_srl, R_TYPE, comparator_17_eq, comparator_18_eq);
  and and_10 (R_or, R_TYPE, comparator_19_eq, comparator_20_eq);
  and and_11 (R_rem, R_TYPE, comparator_21_eq, comparator_22_eq);
  and and_12 (R_and, R_TYPE, comparator_23_eq, comparator_24_eq);
  or or_1 (or_1_out, R_add, I_add);
  or or_2 (or_2_out, R_and, I_and);
  or or_3 (or_3_out, R_or, I_or);
  or or_4 (or_4_out, R_xor, I_xor);
  or or_5 (or_5_out, R_sll, I_sll);
  or or_6 (or_6_out, R_srl, I_srl);
  or or_7 (or_7_out, R_slt, I_slt);
  Register #(.width(32)) PC (.D(PC_1), .en(in_2), .clk(in_2), .Q(out_3));  // open: clr
  Adder #(.width(32)) adder_1 (.a(out_3), .b(32'h1), .out(PC_1));  // open: cin, cout
  Comparator #(.width(3)) comparator_25 (.a(in_1[14:12]), .b(3'b000), .eq(comparator_25_eq));  // open: gt, lt
  Comparator #(.width(3)) comparator_26 (.a(in_1[14:12]), .b(3'b001), .eq(comparator_26_eq));  // open: gt, lt
  Comparator #(.width(3)) comparator_27 (.a(in_1[14:12]), .b(3'b010), .eq(comparator_27_eq));  // open: gt, lt
  Comparator #(.width(3)) comparator_28 (.a(in_1[14:12]), .b(3'b010), .eq(comparator_28_eq));  // open: gt, lt
  Comparator #(.width(3)) comparator_29 (.a(in_1[14:12]), .b(3'b111), .eq(comparator_29_eq));  // open: gt, lt
  Comparator #(.width(3)) comparator_30 (.a(in_1[14:12]), .b(3'b000), .eq(comparator_30_eq));  // open: gt, lt
  Comparator #(.width(3)) comparator_31 (.a(in_1[14:12]), .b(3'b100), .eq(comparator_31_eq));  // open: gt, lt
  Comparator #(.width(3)) comparator_32 (.a(in_1[14:12]), .b(3'b110), .eq(comparator_32_eq));  // open: gt, lt
  and and_13 (I_lb, I_TYPE_LOAD, comparator_25_eq);
  and and_14 (I_lh, I_TYPE_LOAD, comparator_26_eq);
  and and_15 (I_lw, I_TYPE_LOAD, comparator_27_eq);
  and and_16 (S_sw, S_TYPE, comparator_28_eq);
  and and_17 (S_swge, S_TYPE, comparator_29_eq);
  and and_18 (B_beq, B_TYPE, comparator_30_eq);
  and and_19 (B_blt, B_TYPE, comparator_31_eq);
  and and_20 (B_bltu, B_TYPE, comparator_32_eq);
  Priority_Encoder #(.select(4)) priority_encoder_1 (
    .in0(or_1_out), .in1(or_2_out), .in2(or_3_out), .in3(or_4_out), .in4(or_5_out), .in5(or_6_out),
    .in6(R_mul), .in7(R_mulh), .in8(R_div), .in9(R_rem), .in10(or_7_out), .out(ALU_OP));  // open: in11, in12, in13, in14, in15, gs, en_out, en_in
  Comparator #(.width(7)) comparator_33 (.a(in_1[6:0]), .b(7'b0110011), .eq(R_TYPE));  // open: gt, lt
  Comparator #(.width(7)) comparator_34 (.a(in_1[6:0]), .b(7'b0000011), .eq(I_TYPE_LOAD));  // open: gt, lt
  Comparator #(.width(7)) comparator_35 (.a(in_1[6:0]), .b(7'b0010011), .eq(I_TYPE_OTHER));  // open: gt, lt
  Comparator #(.width(7)) comparator_36 (.a(in_1[6:0]), .b(7'b0100011), .eq(S_TYPE));  // open: gt, lt
  Comparator #(.width(7)) comparator_37 (.a(in_1[6:0]), .b(7'b1100011), .eq(B_TYPE));  // open: gt, lt
  Comparator #(.width(7)) comparator_38 (.a(in_1[6:0]), .b(7'b0110111), .eq(U_TYPE_LOAD));  // open: gt, lt
  Comparator #(.width(7)) comparator_39 (.a(in_1[6:0]), .b(7'b1100111), .eq(U_jal));  // open: gt, lt
  Comparator #(.width(7)) comparator_40 (.a(in_1[6:0]), .b(7'b1101111), .eq(I_jalr));  // open: gt, lt
  or or_8 (or_8_out, B_TYPE, U_jal);
  Multiplexer #(.select(2), .width(32)) multiplexer_1 (
    .in0(R1_DATA), .in1(out_3), .in2({32{1'b0}}), .out(ALU_X1), .sel(ALU_X1_SEL));  // open: in3
  Multiplexer #(.select(2), .width(32)) multiplexer_2 (
    .in0(R2_DATA), .in1(Imm_Value), .in2({32{1'b0}}), .out(ALU_X2), .sel(ALU_X2_SEL));  // open: in3
  Priority_Encoder #(.select(2)) priority_encoder_2 (
    .in0(1'b1), .in1(or_8_out), .in2(U_TYPE_LOAD), .out(ALU_X1_SEL));  // open: in3, gs, en_out, en_in
  Priority_Encoder #(.select(2)) priority_encoder_3 (
    .in0(1'b1), .in1(or_9_out), .in2(S_swge), .out(ALU_X2_SEL));  // open: in3, gs, en_out, en_in
  or or_9 (or_9_out, B_TYPE, I_TYPE, U_TYPE, S_sw);
  ALU alu_1 (.in_1(ALU_X1), .in_2(ALU_X2), .in_3(ALU_OP), .out_4(ALU_OUT), .out_5(isEqual));
  Comparator #(.width(3)) comparator_41 (.a(in_1[14:12]), .b(3'b001), .eq(comparator_41_eq));  // open: gt, lt
  Comparator #(.width(7)) comparator_42 (.a(in_1[31:25]), .b({7{1'b0}}), .eq(comparator_42_eq));  // open: gt, lt
  Comparator #(.width(3)) comparator_43 (.a(in_1[14:12]), .b(3'b001), .eq(comparator_43_eq));  // open: gt, lt
  Comparator #(.width(7)) comparator_44 (.a(in_1[31:25]), .b(7'b0000001), .eq(comparator_44_eq));  // open: gt, lt
  Comparator #(.width(3)) comparator_45 (.a(in_1[14:12]), .b(3'b010), .eq(comparator_45_eq));  // open: gt, lt
  Comparator #(.width(7)) comparator_46 (.a(in_1[31:25]), .b({7{1'b0}}), .eq(comparator_46_eq));  // open: gt, lt
  Comparator #(.width(3)) comparator_47 (.a(in_1[14:12]), .b(3'b100), .eq(comparator_47_eq));  // open: gt, lt
  Comparator #(.width(7)) comparator_48 (.a(in_1[31:25]), .b({7{1'b0}}), .eq(comparator_48_eq));  // open: gt, lt
  Comparator #(.width(3)) comparator_49 (.a(in_1[14:12]), .b(3'b100), .eq(comparator_49_eq));  // open: gt, lt
  Comparator #(.width(7)) comparator_50 (.a(in_1[31:25]), .b(7'b0000001), .eq(comparator_50_eq));  // open: gt, lt
  or or_10 (I_TYPE, I_TYPE_LOAD, I_TYPE_OTHER, I_jalr);
  or or_11 (U_TYPE, U_TYPE_LOAD, U_jal);
  and and_21 (I_sll, I_TYPE_OTHER, comparator_41_eq, comparator_42_eq);
  and and_22 (I_mulh, I_TYPE_OTHER, comparator_43_eq, comparator_44_eq);
  and and_23 (I_slt, I_TYPE_OTHER, comparator_45_eq, comparator_46_eq);
  and and_24 (I_xor, I_TYPE_OTHER, comparator_47_eq, comparator_48_eq);
  and and_25 (I_add, I_TYPE_OTHER, comparator_49_eq, comparator_50_eq);
  assign Imm_I = {{20{in_1[31]}}, in_1[31:20]};  // Bit_Extender bit_extender_1
  assign Imm_S = {{20{in_1[31]}}, {in_1[31:25], in_1[11:7]}};  // Bit_Extender bit_extender_2
  assign Imm_B = {{19{in_1[31]}}, {in_1[31], in_1[7], in_1[30:25], in_1[11:8], 1'b0}};  // Bit_Extender bit_extender_3
  assign Imm_J = {{11{in_1[31]}}, {in_1[31], in_1[19:12], in_1[20], in_1[30:21], 1'b0}};  // Bit_Extender bit_extender_4
  Comparator #(.width(3)) comparator_51 (.a(in_1[14:12]), .b(3'b101), .eq(comparator_51_eq));  // open: gt, lt
  Comparator #(.width(7)) comparator_52 (.a(in_1[31:25]), .b({7{1'b0}}), .eq(comparator_52_eq));  // open: gt, lt
  Comparator #(.width(3)) comparator_53 (.a(in_1[14:12]), .b(3'b110), .eq(comparator_53_eq));  // open: gt, lt
  Comparator #(.width(7)) comparator_54 (.a(in_1[31:25]), .b({7{1'b0}}), .eq(comparator_54_eq));  // open: gt, lt
  Comparator #(.width(3)) comparator_55 (.a(in_1[14:12]), .b(3'b110), .eq(comparator_55_eq));  // open: gt, lt
  Comparator #(.width(7)) comparator_56 (.a(in_1[31:25]), .b(7'b0000001), .eq(comparator_56_eq));  // open: gt, lt
  Comparator #(.width(3)) comparator_57 (.a(in_1[14:12]), .b(3'b111), .eq(comparator_57_eq));  // open: gt, lt
  Comparator #(.width(7)) comparator_58 (.a(in_1[31:25]), .b({7{1'b0}}), .eq(comparator_58_eq));  // open: gt, lt
  and and_26 (I_srl, I_TYPE_OTHER, comparator_51_eq, comparator_52_eq);
  and and_27 (I_or, I_TYPE_OTHER, comparator_53_eq, comparator_54_eq);
  and and_28 (I_rem, I_TYPE_OTHER, comparator_55_eq, comparator_56_eq);
  and and_29 (I_and, I_TYPE_OTHER, comparator_57_eq, comparator_58_eq);
  Priority_Encoder priority_encoder_4 (
    .in0(I_TYPE), .in1(U_TYPE_LOAD), .in2(S_TYPE), .in3(B_TYPE), .in4(U_jal), .out(Imm_SEL));  // open: in5, in6, in7, en_in, gs, en_out
  Multiplexer #(.select(3), .width(32)) multiplexer_3 (
    .in0(Imm_I), .in1({in_1[31:12], {12{1'b0}}}), .in2(Imm_S), .in3(Imm_B), .in4(Imm_J), .out(Imm_Value),
    .sel(Imm_SEL));  // open: in5, in6, in7

  // Other names for the same wires on the sheet: IMM_4_1[3:0] = in_1[11:8]; RAM_INSTRUCTION[31:0] = in_1;
  //   RD[4:0] = in_1[11:7]; IMM_11_B = in_1[7]; CLK = in_2; I_TYPE_JUMP = I_jalr; FUNCT3[2:0] = in_1[14:12];
  //   IMM_19_12[7:0] = in_1[19:12]; IMM_31_12[19:0] = in_1[31:12]; Imm_U[31:12] = in_1[31:12]; RS1[4:0] = in_1[19:15];
  //   IMM_11_0[11:0] = in_1[31:20]; IMM_11_J = in_1[20]; RS2[4:0] = in_1[24:20]; IMM_10_1[9:0] = in_1[30:21];
  //   FUNCT7[6:0] = in_1[31:25]; IMM_10_5[5:0] = in_1[30:25]; IMM_11_5[6:0] = in_1[31:25]; IMM_12 = in_1[31];
  //   IMM_20 = in_1[31]; PC[31:0] = out_3; RAM_ADDR[31:0] = out_3; RAM_DATA[31:0] = out_4; OPCODE[6:0] = in_1[6:0];
  //   RAM_WRITE_EN = out_5; U_lui = U_jal; U_TYPE_JUMP = U_jal

  // Notes on the sheet:
  //   REGISTERS
  //   outputs
  //   R-Type
  //   I-Type
  //   U-Type
  //   S-Type
  //   B-Type
  //   J-Type
  //   EXECUTE
  //   IMM_4_0
  //   ALU OP ENCODING
  //   I/O
  //   FETCH
  //   DECODE
  //   INSTRUCTION DECODING
  //   inputs
  //   ALU Input Selection
  //   S-Type
  //   I-Type
  //   U-Type
  //   IMM_4_0
  //   B-Type
  //   J-Type
  //   Immediate Value Selection
endmodule

module REGISTERS (
  input  [4:0] in_1,
  input  [4:0] in_2,
  input  in_3,
  input  [4:0] in_4,
  input  [31:0] in_5,
  input  in_6,
  output [31:0] out_7,
  output [31:0] out_8
);

  wire [31:0] in_r1, in_r2, in_r3, in_r4, in_r5, in_r6, in_r7, in_r8, in_r9, in_r10, in_r11, in_r12, in_r13,
       in_r14, in_r15, in_r16, in_r17, in_r18, in_r19, in_r20, in_r21, in_r22, in_r23, in_r24, in_r25,
       in_r26, in_r27, in_r28, in_r29, in_r30, in_r31, out_r1, out_r2, out_r3, out_r4, out_r5, out_r6,
       out_r7, out_r8, out_r9, out_r10, out_r11, out_r12, out_r13, out_r14, out_r15, out_r16, out_r17,
       out_r18, out_r19, out_r20, out_r21, out_r22, out_r23, out_r24, out_r25, out_r26, out_r27, out_r28,
       out_r29, out_r30, out_r31;

  Demultiplexer #(.enable("true"), .select(5), .width(32)) demultiplexer_1 (
    .out1(in_r1), .out2(in_r2), .out3(in_r3), .out4(in_r4), .out5(in_r5), .out6(in_r6), .out7(in_r7),
    .out8(in_r8), .out9(in_r9), .out10(in_r10), .out11(in_r11), .out12(in_r12), .out13(in_r13),
    .out14(in_r14), .out15(in_r15), .out16(in_r16), .out17(in_r17), .out18(in_r18), .out19(in_r19),
    .out20(in_r20), .out21(in_r21), .out22(in_r22), .out23(in_r23), .out24(in_r24), .out25(in_r25),
    .out26(in_r26), .out27(in_r27), .out28(in_r28), .out29(in_r29), .out30(in_r30), .out31(in_r31),
    .in(in_5), .sel(in_4), .en(in_3));  // open: out0
  Multiplexer #(.select(5), .width(32)) multiplexer_1 (
    .in0({32{1'b0}}), .in1(in_r1), .in2(in_r2), .in3(in_r3), .in4(in_r4), .in5(in_r5), .in6(in_r6),
    .in7(in_r7), .in8(in_r8), .in9(in_r9), .in10(in_r10), .in11(in_r11), .in12(in_r12), .in13(in_r13),
    .in14(in_r14), .in15(in_r15), .in16(in_r16), .in17(in_r17), .in18(in_r18), .in19(in_r19), .in20(in_r20),
    .in21(in_r21), .in22(in_r22), .in23(in_r23), .in24(in_r24), .in25(in_r25), .in26(in_r26), .in27(in_r27),
    .in28(in_r28), .in29(in_r29), .in30(in_r30), .in31(in_r31), .out(out_7), .sel(in_1));
  Multiplexer #(.select(5), .width(32)) multiplexer_2 (
    .in0({32{1'b0}}), .in1(in_r1), .in2(in_r2), .in3(in_r3), .in4(in_r4), .in5(in_r5), .in6(in_r6),
    .in7(in_r7), .in8(in_r8), .in9(in_r9), .in10(in_r10), .in11(in_r11), .in12(in_r12), .in13(in_r13),
    .in14(in_r14), .in15(in_r15), .in16(in_r16), .in17(in_r17), .in18(in_r18), .in19(in_r19), .in20(in_r20),
    .in21(in_r21), .in22(in_r22), .in23(in_r23), .in24(in_r24), .in25(in_r25), .in26(in_r26), .in27(in_r27),
    .in28(in_r28), .in29(in_r29), .in30(in_r30), .in31(in_r31), .out(out_8), .sel(in_2));
  Register #(.width(32)) r1 (.D(in_r1), .en(in_3), .clk(in_6), .Q(out_r1));  // open: clr
  Register #(.width(32)) r5 (.D(in_r5), .en(in_3), .clk(in_6), .Q(out_r5));  // open: clr
  Register #(.width(32)) r9 (.D(in_r9), .en(in_3), .clk(in_6), .Q(out_r9));  // open: clr
  Register #(.width(32)) r13 (.D(in_r13), .en(in_3), .clk(in_6), .Q(out_r13));  // open: clr
  Register #(.width(32)) r17 (.D(in_r17), .en(in_3), .clk(in_6), .Q(out_r17));  // open: clr
  Register #(.width(32)) r21 (.D(in_r21), .en(in_3), .clk(in_6), .Q(out_r21));  // open: clr
  Register #(.width(32)) r25 (.D(in_r25), .en(in_3), .clk(in_6), .Q(out_r25));  // open: clr
  Register #(.width(32)) r29 (.D(in_r29), .en(in_3), .clk(in_6), .Q(out_r29));  // open: clr
  Register #(.width(32)) r2 (.D(in_r2), .en(in_3), .clk(in_6), .Q(out_r2));  // open: clr
  Register #(.width(32)) r6 (.D(in_r6), .en(in_3), .clk(in_6), .Q(out_r6));  // open: clr
  Register #(.width(32)) r10 (.D(in_r10), .en(in_3), .clk(in_6), .Q(out_r10));  // open: clr
  Register #(.width(32)) r14 (.D(in_r14), .en(in_3), .clk(in_6), .Q(out_r14));  // open: clr
  Register #(.width(32)) r18 (.D(in_r18), .en(in_3), .clk(in_6), .Q(out_r18));  // open: clr
  Register #(.width(32)) r22 (.D(in_r22), .en(in_3), .clk(in_6), .Q(out_r22));  // open: clr
  Register #(.width(32)) r26 (.D(in_r26), .en(in_3), .clk(in_6), .Q(out_r26));  // open: clr
  Register #(.width(32)) r30 (.D(in_r30), .en(in_3), .clk(in_6), .Q(out_r30));  // open: clr
  Register #(.width(32)) r3 (.D(in_r3), .en(in_3), .clk(in_6), .Q(out_r3));  // open: clr
  Register #(.width(32)) r7 (.D(in_r7), .en(in_3), .clk(in_6), .Q(out_r7));  // open: clr
  Register #(.width(32)) r11 (.D(in_r11), .en(in_3), .clk(in_6), .Q(out_r11));  // open: clr
  Register #(.width(32)) r15 (.D(in_r15), .en(in_3), .clk(in_6), .Q(out_r15));  // open: clr
  Register #(.width(32)) r19 (.D(in_r19), .en(in_3), .clk(in_6), .Q(out_r19));  // open: clr
  Register #(.width(32)) r23 (.D(in_r23), .en(in_3), .clk(in_6), .Q(out_r23));  // open: clr
  Register #(.width(32)) r27 (.D(in_r27), .en(in_3), .clk(in_6), .Q(out_r27));  // open: clr
  Register #(.width(32)) r31 (.D(in_r31), .en(in_3), .clk(in_6), .Q(out_r31));  // open: clr
  Register #(.width(32)) r4 (.D(in_r4), .en(in_3), .clk(in_6), .Q(out_r4));  // open: clr
  Register #(.width(32)) r8 (.D(in_r8), .en(in_3), .clk(in_6), .Q(out_r8));  // open: clr
  Register #(.width(32)) r12 (.D(in_r12), .en(in_3), .clk(in_6), .Q(out_r12));  // open: clr
  Register #(.width(32)) r16 (.D(in_r16), .en(in_3), .clk(in_6), .Q(out_r16));  // open: clr
  Register #(.width(32)) r20 (.D(in_r20), .en(in_3), .clk(in_6), .Q(out_r20));  // open: clr
  Register #(.width(32)) r24 (.D(in_r24), .en(in_3), .clk(in_6), .Q(out_r24));  // open: clr
  Register #(.width(32)) r28 (.D(in_r28), .en(in_3), .clk(in_6), .Q(out_r28));  // open: clr

  // Other names for the same wires on the sheet: CLK = in_6; reg1[4:0] = in_1; reg1_data[31:0] = out_7;
  //   reg2[4:0] = in_2; reg2_data[31:0] = out_8; reg_wr[4:0] = in_4; reg_wr_data[31:0] = in_5; write_enable = in_3

  // Notes on the sheet:
  //   register write
  //   outputs
  //   I/O
  //   inputs
  //   register read
endmodule

module ALU (
  input  [31:0] in_1,
  input  [31:0] in_2,
  input  [3:0] in_3,
  output [31:0] out_4,
  output out_5
);

  wire comparator_1_lt;
  wire [31:0] o_add, o_and, o_div, o_mul, o_mulh, o_or, o_rem, o_sll, o_slt, o_srl, o_sub, o_xor;

  Adder #(.width(32)) adder_1 (.a(in_1), .b(in_2), .out(o_add));  // open: cin, cout
  Subtractor #(.width(32)) subtractor_1 (.a(in_1), .b(in_2), .out(o_sub));  // open: bin, bout
  assign o_and = in_1 & in_2;  // AND_Gate and_1, 32 bits wide
  assign o_or = in_1 | in_2;  // OR_Gate or_1, 32 bits wide
  assign o_xor = in_1 ^ in_2;  // XOR_Gate xor_1, 32 bits wide
  Shifter #(.shift("lr"), .width(32)) shifter_1 (.in(in_1), .\dist (in_2[4:0]), .out(o_sll));
  Comparator #(.width(32)) comparator_1 (.a(in_1), .b(in_2), .lt(comparator_1_lt));  // open: gt, eq
  assign o_slt = {{31{comparator_1_lt}}, comparator_1_lt};  // Bit_Extender bit_extender_1
  Shifter #(.width(32)) shifter_2 (.in(in_1), .\dist (in_2[4:0]), .out(o_srl));
  Multiplier #(.width(32)) multiplier_1 (.a(in_1), .b(in_2), .out(o_mul));  // open: cin, cout
  Multiplier #(.width(32)) multiplier_2 (.a(in_1), .b(in_2), .cout(o_mulh));  // open: out, cin
  Divider #(.width(32)) divider_1 (.a(in_1), .b(in_2), .out(o_div));  // open: upper, rem
  Divider #(.width(32)) divider_2 (.a(in_1), .b(in_2), .rem(o_rem));  // open: out, upper
  Multiplexer #(.select(4), .width(32)) multiplexer_1 (
    .in0(o_add), .in1(o_sub), .in2(o_and), .in3(o_or), .in4(o_xor), .in5(o_sll), .in6(o_srl), .in7(o_mul),
    .in8(o_mulh), .in9(o_div), .in10(o_rem), .in11(o_slt), .out(out_4), .sel(in_3));  // open: in12, in13, in14, in15

  // Other names for the same wires on the sheet: isEqual = out_5; op[3:0] = in_3; result[31:0] = out_4;
  //   x[31:0] = in_1; y[31:0] = in_2

  // Notes on the sheet:
  //   outputs
  //   I/O
  //   inputs
  //   OPERATIONS
  //   OPERATION SELECTION
endmodule
